// Logisim project tut_2.circ as structural Verilog: 11 circuits, main circuit SR_Circuits
module SR_Circuits (
);

  wire clocked_sr_latch_nor_1_q, clocked_sr_latch_nor_1_qnot, dipswitch_2_sw1, R, S, sr_latch_nand_1_q,
       sr_latch_nand_1_qnot, sr_latch_nor_1_q, sr_latch_nor_1_qnot;

  DipSwitch #(.number(2)) dipswitch_1 (.sw1(S), .sw2(R));
  DipSwitch #(.number(1)) dipswitch_2 (.sw1(dipswitch_2_sw1));
  LED led_1 (.in(sr_latch_nor_1_q));
  SR_Latch_NOR sr_latch_nor_1 (.R(R), .S(S), .Q(sr_latch_nor_1_q), .Qnot(sr_latch_nor_1_qnot));
  LED led_2 (.in(sr_latch_nor_1_qnot));
  LED led_3 (.in(sr_latch_nand_1_q));
  SR_Latch_NAND sr_latch_nand_1 (.S(S), .R(R), .Q(sr_latch_nand_1_q), .Qnot(sr_latch_nand_1_qnot));
  LED led_4 (.in(sr_latch_nand_1_qnot));
  LED led_5 (.in(clocked_sr_latch_nor_1_q));
  Clocked_SR_Latch_NOR clocked_sr_latch_nor_1 (
    .R(R), .E(dipswitch_2_sw1), .S(S), .Q(clocked_sr_latch_nor_1_q), .Qnot(clocked_sr_latch_nor_1_qnot));
  LED led_6 (.in(clocked_sr_latch_nor_1_qnot));
endmodule

module Clocked_SR_Latch_NOR (
  input  R,
  input  E,
  input  S,
  output Q,
  output Qnot
);

  wire and_1_out, and_2_out;

  and and_1 (and_1_out, R, E);
  and and_2 (and_2_out, E, S);
  SR_Latch_NOR sr_latch_nor_1 (.R(and_1_out), .S(and_2_out), .Q(Q), .Qnot(Qnot));
endmodule

module SR_Latch_NOR (
  input  R,
  input  S,
  output Q,
  output Qnot
);

  nor nor_1 (Q, R, Qnot);
  nor nor_2 (Qnot, Q, S);
endmodule

module SR_Latch_NAND (
  input  S,
  input  R,
  output Q,
  output Qnot
);

  nand nand_1 (Q, S, Qnot);
  nand nand_2 (Qnot, Q, R);
endmodule

module D_Latch (
  input  E,
  input  D,
  output Q,
  output Qnot
);

  wire not_1_out;

  not not_1 (not_1_out, D);
  Clocked_SR_Latch_NOR clocked_sr_latch_nor_1 (.R(not_1_out), .E(E), .S(D), .Q(Q), .Qnot(Qnot));
endmodule

module D_Circuits (
);

  wire button_1_out, button_2_out, CLK, d_flip_flop_1_q, d_flip_flop_1_qnot, d_latch_1_q, d_latch_1_qnot,
       dipswitch_1_sw1, dipswitch_1_sw2, t_flip_flop_1_q, t_flip_flop_1_qnot;

  DipSwitch #(.number(2)) dipswitch_1 (.sw1(dipswitch_1_sw1), .sw2(dipswitch_1_sw2));
  Button button_1 (.out(button_1_out));
  Button button_2 (.out(button_2_out));
  Clock clock_1 (.out(CLK));
  D_Latch d_latch_1 (.E(dipswitch_1_sw1), .D(dipswitch_1_sw2), .Q(d_latch_1_q), .Qnot(d_latch_1_qnot));
  D_Flip_Flop d_flip_flop_1 (.CLK(CLK), .D(button_1_out), .Q(d_flip_flop_1_q), .Qnot(d_flip_flop_1_qnot));
  T_Flip_Flop t_flip_flop_1 (.CLK(CLK), .T(button_2_out), .Q(t_flip_flop_1_q), .Qnot(t_flip_flop_1_qnot));
  LED led_1 (.in(d_latch_1_q));
  LED led_2 (.in(d_latch_1_qnot));
  LED led_3 (.in(d_flip_flop_1_q));
  LED led_4 (.in(d_flip_flop_1_qnot));
  LED led_5 (.in(t_flip_flop_1_q));
  LED led_6 (.in(t_flip_flop_1_qnot));
endmodule

module D_Flip_Flop (
  input  CLK,
  input  D,
  output Q,
  output Qnot
);

  wire d_latch_1_q, not_1_out, not_2_out;

  not not_1 (not_1_out, CLK);
  not not_2 (not_2_out, not_1_out);
  D_Latch d_latch_1 (.E(not_1_out), .D(D), .Q(d_latch_1_q));  // open: Qnot
  D_Latch d_latch_2 (.E(not_2_out), .D(d_latch_1_q), .Q(Q), .Qnot(Qnot));
endmodule

module T_Flip_Flop (
  input  CLK,
  input  T,
  output Q,
  output Qnot
);

  wire xor_1_out;

  xor xor_1 (xor_1_out, Q, T);
  D_Flip_Flop d_flip_flop_1 (.CLK(CLK), .D(xor_1_out), .Q(Q), .Qnot(Qnot));
endmodule

module Shift_Register (
  input  DATA_IN,
  input  M,
  input  CLK,
  output Q0,
  output Q1,
  output Q2,
  output Q3
);

  wire D0, D1, D2, D3;

  D_Flip_Flop d_flip_flop_1 (.CLK(CLK), .D(D0), .Q(Q0));  // open: Qnot
  Multiplexer multiplexer_1 (.in0(DATA_IN), .in1(Q1), .out(D0), .sel(M));
  Multiplexer multiplexer_2 (.in0(Q1), .in1(Q3), .out(D2), .sel(M));
  D_Flip_Flop d_flip_flop_2 (.CLK(CLK), .D(D1), .Q(Q1));  // open: Qnot
  Multiplexer multiplexer_3 (.in0(Q0), .in1(Q2), .out(D1), .sel(M));
  Multiplexer multiplexer_4 (.in0(Q2), .in1(DATA_IN), .out(D3), .sel(M));
  D_Flip_Flop d_flip_flop_3 (.CLK(CLK), .D(D2), .Q(Q2));  // open: Qnot
  D_Flip_Flop d_flip_flop_4 (.CLK(CLK), .D(D3), .Q(Q3));  // open: Qnot
endmodule

module Shift_Demo (
);

  wire button_1_out, clock_1_out, dipswitch_1_sw1, Q0, Q1, Q2, Q3;

  Button button_1 (.out(button_1_out));
  DipSwitch #(.number(1)) dipswitch_1 (.sw1(dipswitch_1_sw1));
  Clock clock_1 (.out(clock_1_out));
  Shift_Register shift_register_1 (
    .DATA_IN(button_1_out), .M(dipswitch_1_sw1), .CLK(clock_1_out), .Q0(Q0), .Q1(Q1), .Q2(Q2), .Q3(Q3));
  LED led_1 (.in(Q0));
  LED led_2 (.in(Q1));
  LED led_3 (.in(Q2));
  LED led_4 (.in(Q3));
endmodule

module Register_File (
  input  WriteEnable,
  input  [15:0] WriteData,
  input  [1:0] WriteReg,
  input  [1:0] ReadReg0,
  input  [1:0] ReadReg1,
  input  [1:0] ReadReg2,
  input  [1:0] ReadReg3,
  output [15:0] ReadData0,
  output [15:0] ReadData1,
  output [15:0] ReadData2,
  output [15:0] ReadData3
);

  wire decoder_1_out0, decoder_1_out1, decoder_1_out2, decoder_1_out3;
  wire [15:0] Reg0, Reg1, Reg2, Reg3;

  Decoder #(.select(2)) decoder_1 (
    .out0(decoder_1_out0), .out1(decoder_1_out1), .out2(decoder_1_out2), .out3(decoder_1_out3),
    .sel(WriteReg), .en(WriteEnable));
  Multiplexer #(.select(2), .width(16)) multiplexer_1 (
    .in0(Reg0), .in1(Reg1), .in2(Reg2), .in3(Reg3), .out(ReadData0), .sel(ReadReg0));
  Multiplexer #(.select(2), .width(16)) multiplexer_2 (
    .in0(Reg0), .in1(Reg1), .in2(Reg2), .in3(Reg3), .out(ReadData1), .sel(ReadReg1));
  Multiplexer #(.select(2), .width(16)) multiplexer_3 (
    .in0(Reg0), .in1(Reg1), .in2(Reg2), .in3(Reg3), .out(ReadData2), .sel(ReadReg2));
  Multiplexer #(.select(2), .width(16)) multiplexer_4 (
    .in0(Reg0), .in1(Reg1), .in2(Reg2), .in3(Reg3), .out(ReadData3), .sel(ReadReg3));
  Register #(.width(16)) register_1 (.D(WriteData), .en(decoder_1_out0), .clk(WriteEnable), .Q(Reg0));  // open: clr
  Register #(.width(16)) register_2 (.D(WriteData), .en(decoder_1_out1), .clk(WriteEnable), .Q(Reg1));  // open: clr
  Register #(.width(16)) register_3 (.D(WriteData), .en(decoder_1_out2), .clk(WriteEnable), .Q(Reg2));  // open: clr
  Register #(.width(16)) register_4 (.D(WriteData), .en(decoder_1_out3), .clk(WriteEnable), .Q(Reg3));  // open: clr

  // Other names for the same wires on the sheet: CLK = WriteEnable; D[15:0] = WriteData
endmodule
